# Fritzing sketch arduino_nano (saved by Fritzing 0.9.3b)
breadboards: 1

parts:
  Nano1 = Arduino Nano v2.3
  U2 = SN74LS14N [package="DIP14 [THT]"]

nets:
  GND: Nano1.GND, U2.GND
  N1: Nano1.D2, U2.1A
  N2: Nano1.D3, U2.1Y
  N3: Nano1.D4, U2.2A
  N4: Nano1.D5, U2.6A
  N5: Nano1.D6, U2.6Y
  N6: Nano1.D7, U2.5A
  N7: Nano1.A3, U2.3Y
  N8: Nano1.A2, U2.3A
  N9: Nano1.A1, U2.2Y
